# Fritzing sketch lcd-batterymeter-schematic (saved by Fritzing 0.9.3b)
breadboards: 1

parts:
  Arduino = Arduino Uno (Rev3)
  1602 = LCD screen
  cell_for_testing = LIPO-1000mAh [package=lipo-1000]
  5k_contrast_pot = TRIMPOT [package=3386u]
  Q1 = Basic FET N-Channel [package="DPak [SMD]"]
  Q2 = Basic FET N-Channel [package="DPak [SMD]"]
  Bulb = Resistor [tolerance=±5% resistance=5 package=THT]
  Bulb_2 = Resistor [tolerance=±5% resistance=5 package=THT]
  Shunt_resistor = Resistor [tolerance=±5% resistance=1 package=THT]
  pulldown_resistor = Resistor [tolerance=±5% resistance=10k package=THT]

nets:
  N1: Arduino.A0, Q1.drain, Q2.drain, Shunt_resistor.Pin_0
  N2: Arduino.A1, cell_for_testing.+, Shunt_resistor.Pin_1, pulldown_resistor.Pin_0
  N3: Arduino.D8, Q2.Gate
  N4: Arduino.D9_PWM, Q1.Gate
  GND: Arduino.GND, 1602.VSS, 1602.R/W, 1602.LED-, cell_for_testing.-, 5k_contrast_pot.CW, Bulb.Pin_1, Bulb_2.Pin_1, pulldown_resistor.Pin_1
  N5: Arduino.D0/RX, 1602.RS
  N6: Arduino.D1/TX, 1602.E
  N7: Arduino.D4, 1602.DB4
  N8: Arduino.D5_PWM, 1602.DB5
  N9: Arduino.D6_PWM, 1602.DB6
  N10: Arduino.D7, 1602.DB7
  5V: Arduino.5V, 1602.VDD, 1602.LED+, 5k_contrast_pot.CCW
  N11: 1602.V0, 5k_contrast_pot.WIPER
  N12: Q1.source, Bulb_2.Pin_0
  N13: Q2.source, Bulb.Pin_0

notes:
  Power supply not shown.
  use USB connector for power
